# Fritzing sketch ArduinoTMP (saved by Fritzing 0.9.0b)
breadboards: 1

parts:
  Part1 = Arduino Uno (Rev3) - ICSP
  U1 = TMP36 [package=to-92-kit]

nets:
  N1: Part1.A0, U1.VOUT
  5V: Part1.5V, U1.VCC
  GND: Part1.GND, U1.GND

notes:
  TMP36 circuit
