# Fritzing sketch ArduinoTMP_LED_LED3 (saved by Fritzing 0.9.0b)
breadboards: 1

parts:
  Part1 = Arduino Uno (Rev3) - ICSP
  U1 = TMP36 [package=to-92-kit]
  R1 = Resistor [tolerance=±5% resistance=220 package=THT]
  LED2 = RGB LED (com. cathode, rbg) [package="5 mm [THT]"]  # not connected

nets:
  N1: Part1.A0, U1.VOUT
  5V: Part1.5V, U1.VCC
  GND: Part1.GND, U1.GND, R1.Pin_0
